// Logisim project lab1.circ as structural Verilog: 1 circuit, main circuit main
module main (
  input  A2,
  input  C1,
  input  A1,
  input  B2,
  input  C2,
  input  B1
);

  wire and_1_out, and_2_out, and_3_out, and_4_out, and_5_out, nor_1_out, not_1_out, not_2_out, not_3_out,
       or_2_out, or_3_out, xor_1_out, xor_2_out;

  not not_1 (not_1_out, A1);
  and and_1 (and_1_out, B2, A1);
  not not_2 (not_2_out, B1);
  xor xor_1 (xor_1_out, A2, B2);
  not not_3 (not_3_out, xor_1_out);
  xor xor_2 (xor_2_out, A1, B1);
  nor nor_1 (nor_1_out, B2, A2);
  and and_2 (and_2_out, A2, B1);
  and and_3 (and_3_out, not_3_out, A1);
  and and_4 (and_4_out, and_1_out, not_2_out);
  and and_5 (and_5_out, not_1_out, and_2_out);
  or or_1 (C1, and_3_out, xor_2_out);
  or or_2 (or_2_out, nor_1_out, and_4_out);
  or or_3 (or_3_out, or_2_out, and_5_out);
  not not_4 (C2, or_3_out);
endmodule
