// Logisim project lab2.circ as structural Verilog: 1 circuit, main circuit main
module main (
  input  in_1,
  input  A1,
  input  A0,
  input  B1,
  input  B0,
  input  S0,
  input  S1,
  input  X0,
  output X2,
  output X1,
  output X0_2
);

  wire and_1_out, and_2_out, and_3_out, and_4_out, and_5_out, not_1_out, not_2_out, not_3_out, or_1_out,
       or_2_out, or_3_out, or_4_out, xor_1_out, xor_2_out;

  and and_1 (and_1_out, A0, B0);
  or or_1 (or_1_out, B1, A1);
  and and_2 (and_2_out, B1, A1);
  not not_1 (not_1_out, A0);
  or or_2 (or_2_out, not_1_out, not_2_out);
  not not_2 (not_2_out, B0);
  and and_3 (and_3_out, and_1_out, or_1_out);
  not not_3 (not_3_out, xor_1_out);
  xor xor_1 (xor_1_out, B1, A1);
  or or_3 (or_3_out, and_3_out, and_2_out);
  and and_4 (and_4_out, and_1_out, not_3_out);
  and and_5 (and_5_out, xor_1_out, or_2_out);
  or or_4 (or_4_out, and_4_out, and_5_out);
  xor xor_2 (xor_2_out, A0, B0);
  // _4_to_1_MUX__x2___74153 #(.Facing("east")) 4_to_1_mux_x2_74153_1: pin names not known; wires that end beside it: 1'b1, A1, B1, or_3_out, 1'b1, A0, B0, or_4_out, in_1, S0, in_1, S1, X2, X1
  // _4_to_1_MUX__x2___74153 #(.Facing("east")) 4_to_1_mux_x2_74153_2: pin names not known; wires that end beside it: S1, S1, S1, xor_2_out, X0, S0, S1, X0_2
endmodule
